# Fritzing sketch FLIPDOTS (saved by Fritzing 0.9.5d)

parts:
  U4 = ESP32S-HiLetgo [part_number=ESP32S-HiLetgo]
  U5 = Mini-360 DC-DC Buck converter [package=THT]
  Power_plug1 = Power plug
  RS485_module2 = RS485 Module (MAX3485)
  IC1 = IC, SIP package, 4 pins [chip_label="Alfa-Zeta Flipdot"]

nets:
  N1: U4.3.3, U5.OUT+, RS485_module2.VCC, RS485_module2.RE, RS485_module2.DE
  N2: U4.GPIO17, RS485_module2.DI
  GND: U4.GND, U5.OUT-, RS485_module2.GND
  N3: U5.IN-, Power_plug1.GND, IC1.pin4
  N4: U5.IN+, Power_plug1.VCC, IC1.pin3
  N5: RS485_module2.A, IC1.pin1
  N6: RS485_module2.B, IC1.pin2

notes:
  24v in
  3.3v out

custom parts:
  ESP32S-HiLetgo: HiLetgo ESP-WROOM-32 ESP32 ESP-32S Development Board 2.4GHz Dual-Mode WiFi + Bluetooth Dual Cores Microcontroller The ESP32 integrated with Antenna switches, RF Balun, power amplifiers, low-noise amplifiers, filters, and management modules, and the entire solution occupies the least area of PCB. 2.4 GHz Wi-Fi plus Bluetooth dual-mode chip, with TSMC Ultra-low power consumption 40nm technology,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
  Mini-360 DC-DC Buck converter: Mini-360 DC-DC Buck converter. Tiny buck step down voltage converter, input voltage 4.75 to 23V output 1 to 17V adjustable. Available from ebay and the like.
  RS485 Module (MAX3485): Commercially available RS485 to RS232 TTL Module
